// Digital circuit 00-ALU-01.dig as structural Verilog
module _00_ALU_01 (
  input  [15:0] A,
  input  [15:0] B,
  input  [1:0] sel,
  output [15:0] S,
  output C_out,
  output ZF
);

  wire add_1_c_o, sub_1_c_o;
  wire [15:0] add_1_s, and_1_out, or_1_out, sub_1_s;

  Add #(.Bits(16)) add_1 (.a(A), .b(B), .c_i(1'b0), .s(add_1_s), .c_o(add_1_c_o));
  Sub #(.Bits(16)) sub_1 (.a(A), .b(B), .c_i(1'b0), .s(sub_1_s), .c_o(sub_1_c_o));
  assign and_1_out = A & B;  // And and_1, 16 bits wide
  assign or_1_out = A | B;  // Or or_1, 16 bits wide
  Comparator #(.Bits(16)) comparator_1 (.a(A), .b(B), .eq(ZF));  // open: gt, lt
  Multiplexer #(.Selector_Bits(2), .Bits(16)) multiplexer_1 (
    .sel(sel), .in_0(add_1_s), .in_1(sub_1_s), .in_2(and_1_out), .in_3(or_1_out), .out(S));
  Multiplexer multiplexer_2 (.sel(sel[0]), .in_0(add_1_c_o), .in_1(sub_1_c_o), .out(C_out));

  // Other names for the same wires on the sheet: sel0[1:0] = sel
endmodule
