// Digital circuit 00-ALU-02-最初的计算单元.dig as structural Verilog
module \_00_ALU_02_最初的计算单元  (
  input  [15:0] B,
  input  [1:0] sel,
  input  en,
  output [15:0] S
);

  wire C_out;
  wire [15:0] _00_alu_01_1_s;

  Button C (.out(C_out));
  Register #(.Bits(16)) register_1 (.D(_00_alu_01_1_s), .C(C_out), .en(en), .Q(S));
  _00_ALU_01 _00_alu_01_1 (.A(S), .B(B), .sel(sel), .S(_00_alu_01_1_s));  // open: C_out, ZF
endmodule
