// Digital circuit 00-ALU-04-组合cpu-添加计数器.dig as structural Verilog
module \_00_ALU_04_组合cpu_添加计数器  (
  input  [15:0] D_in,
  input  [1:0] sel,
  input  en,
  input  str,
  input  ld,
  output [15:0] S
);

  wire C_out;
  wire [1:0] \_05_2位计数器_1_d_out ;
  wire [15:0] _00_alu_01_1_s, eepromdualport_1_d;

  Button C (.out(C_out));
  \_05_2位计数器  \_05_2位计数器_1  (.en(en), .C(C_out), .D_out(\_05_2位计数器_1_d_out ));  // open: ovf
  EEPROMDualPort #(.Bits(16)) eepromdualport_1 (
    .A(\_05_2位计数器_1_d_out ), .Din(D_in), .str(str), .C(C_out), .ld(ld), .D(eepromdualport_1_d));
  Register #(.Bits(16)) register_1 (.D(_00_alu_01_1_s), .C(C_out), .en(en), .Q(S));
  _00_ALU_01 _00_alu_01_1 (.A(S), .B(eepromdualport_1_d), .sel(sel), .S(_00_alu_01_1_s));  // open: C_out, ZF

  // Notes on the sheet:
  //   contents of eepromdualport_1 (hex, n*v repeats v):
  //   14,1e,28,32
endmodule
