// Digital circuit 00-ALU-05-组合cpu-添加halt信号停止计算.dig as structural Verilog
module \_00_ALU_05_组合cpu_添加halt信号停止计算  (
  input  [15:0] D_in,
  input  [1:0] sel,
  input  en,
  input  str,
  input  ld,
  input  C,
  output [15:0] S
);

  wire C_t, comparator_1_lt;
  wire [2:0] D_out;
  wire [15:0] _00_alu_01_1_s, eepromdualport_1_d;

  Comparator #(.Bits(3)) comparator_1 (.a(D_out), .b(3'b100), .lt(comparator_1_lt));  // open: gt, eq
  and and_1 (C_t, C, comparator_1_lt);
  \_05_3位计数器  \_05_3位计数器_1  (.en(en), .C(C_t), .D_out(D_out));  // open: ovf
  EEPROMDualPort #(.AddrBits(3), .Bits(16)) eepromdualport_1 (
    .A(D_out), .Din(D_in), .str(str), .C(C_t), .ld(ld), .D(eepromdualport_1_d));
  Register #(.Bits(16)) register_1 (.D(_00_alu_01_1_s), .C(C_t), .en(en), .Q(S));
  _00_ALU_01 _00_alu_01_1 (.A(S), .B(eepromdualport_1_d), .sel(sel), .S(_00_alu_01_1_s));  // open: C_out, ZF

  // Notes on the sheet:
  //   contents of eepromdualport_1 (hex, n*v repeats v):
  //   14,1e,28,32
endmodule
