// Digital circuit 00-ALU-06-组合cpu-完整自动化计算单元.dig as structural Verilog
module \_00_ALU_06_组合cpu_完整自动化计算单元  (
  input  en,
  input  C,
  input  [15:0] D_in,
  input  str,
  input  ld,
  output [15:0] S
);

  wire C_t, comparator_1_lt;
  wire [2:0] D_out;
  wire [15:0] _00_alu_01_1_s, eepromdualport_1_d, eepromdualport_2_d;

  Comparator #(.Bits(3)) comparator_1 (.a(D_out), .b(3'b100), .lt(comparator_1_lt));  // open: gt, eq
  and and_1 (C_t, C, comparator_1_lt);
  \_05_3位计数器  \_05_3位计数器_1  (.en(en), .C(C_t), .D_out(D_out));  // open: ovf
  EEPROMDualPort #(.AddrBits(3), .Bits(16)) eepromdualport_1 (
    .A(D_out), .Din(D_in), .str(str), .C(C_t), .ld(ld), .D(eepromdualport_1_d));
  EEPROMDualPort #(.AddrBits(3), .Bits(16)) eepromdualport_2 (
    .A(D_out), .Din(D_in), .str(str), .C(C_t), .ld(ld), .D(eepromdualport_2_d));
  Register #(.Bits(16)) register_1 (.D(_00_alu_01_1_s), .C(C_t), .en(en), .Q(S));
  _00_ALU_01 _00_alu_01_1 (
    .A(S), .B(eepromdualport_1_d), .sel(eepromdualport_2_d[1:0]), .S(_00_alu_01_1_s));  // open: C_out, ZF

  // Notes on the sheet:
  //   C: Hz: 100
  //   contents of eepromdualport_1 (hex, n*v repeats v):
  //   14,1e,28,32
  //   contents of eepromdualport_2 (hex, n*v repeats v):
  //   0,0,1
endmodule
