// Digital circuit 00-ALU-07-组合cpu-编写控制指令halt信号.dig as structural Verilog
module \_00_ALU_07_组合cpu_编写控制指令halt信号  (
  input  en,
  input  C,
  input  [15:0] D_in,
  input  str,
  input  ld,
  output [15:0] S
);

  wire C_t, halt;
  wire [2:0] D_out;
  wire [14:0] eepromdualport_2_d;
  wire [15:0] _00_alu_01_1_s, eepromdualport_1_d;

  and and_1 (C_t, C, halt);
  \_05_3位计数器  \_05_3位计数器_1  (.en(en), .C(C_t), .D_out(D_out));  // open: ovf
  EEPROMDualPort #(.AddrBits(3), .Bits(16)) eepromdualport_1 (
    .A(D_out), .Din(D_in), .str(str), .C(C_t), .ld(ld), .D(eepromdualport_1_d));
  EEPROMDualPort #(.AddrBits(3), .Bits(16)) eepromdualport_2 (
    .A(D_out), .Din(D_in), .str(str), .C(C_t), .ld(ld), .D({halt, eepromdualport_2_d}));
  Register #(.Bits(16)) register_1 (.D(_00_alu_01_1_s), .C(C_t), .en(en), .Q(S));
  _00_ALU_01 _00_alu_01_1 (
    .A(S), .B(eepromdualport_1_d), .sel(eepromdualport_2_d[1:0]), .S(_00_alu_01_1_s));  // open: C_out, ZF

  // Notes on the sheet:
  //   contents of eepromdualport_1 (hex, n*v repeats v):
  //   14,1e,28,32
  //   contents of eepromdualport_2 (hex, n*v repeats v):
  //   8000,8000,8001,8000
endmodule
