// Digital circuit 00-ALU-08-组合cpu-编写str输入使能信号存储计算结果.dig as structural Verilog
module \_00_ALU_08_组合cpu_编写str输入使能信号存储计算结果  (
  input  en,
  input  C,
  input  [15:0] D0_in,
  input  str0,
  input  ld,
  output [15:0] S
);

  wire and_2_out, C_t, halt, str;
  wire [2:0] D_out;
  wire [14:0] eepromdualport_2_d;
  wire [15:0] _00_alu_01_1_s, eepromdualport_1_d;

  and and_1 (C_t, C, halt);
  \_05_3位计数器  \_05_3位计数器_1  (.en(en), .C(C_t), .D_out(D_out));  // open: ovf
  and and_2 (and_2_out, en, str);
  EEPROMDualPort #(.AddrBits(3), .Bits(16)) eepromdualport_1 (
    .A(D_out), .Din(S), .str(and_2_out), .C(C_t), .ld(ld), .D(eepromdualport_1_d));
  EEPROMDualPort #(.AddrBits(3), .Bits(16)) eepromdualport_2 (
    .A(D_out), .Din(D0_in), .str(str0), .C(C_t), .ld(ld),
    .D({halt, eepromdualport_2_d[14:12], str, eepromdualport_2_d[10:0]}));
  Register #(.Bits(16)) register_1 (.D(_00_alu_01_1_s), .C(C_t), .en(en), .Q(S));
  _00_ALU_01 _00_alu_01_1 (
    .A(S), .B(eepromdualport_1_d), .sel(eepromdualport_2_d[1:0]), .S(_00_alu_01_1_s));  // open: C_out, ZF

  // Other names for the same wires on the sheet: D_in[15:0] = S

  // Notes on the sheet:
  //   contents of eepromdualport_1 (hex, n*v repeats v):
  //   1e,28,32,3c,50
  //   contents of eepromdualport_2 (hex, n*v repeats v):
  //   8000,8000,8001,8000,8800
endmodule
