// Digital circuit 00-ALU-09-组合cpu-编写ld输出信号及selB解决高阻态.dig as structural Verilog
module \_00_ALU_09_组合cpu_编写ld输出信号及selB解决高阻态  (
  input  en,
  input  C,
  input  [15:0] D0_in,
  input  str0,
  input  ld_0,
  output [15:0] S
);

  wire and_2_out, C_t, halt, ld, str;
  wire [1:0] sel_B;
  wire [2:0] D_out;
  wire [14:0] \指令存储_d ;
  wire [15:0] _00_alu_01_1_s, multiplexer_1_out, \数据存储_d ;

  and and_1 (C_t, C, halt);
  \_05_3位计数器  \_05_3位计数器_1  (.en(en), .C(C_t), .D_out(D_out));  // open: ovf
  and and_2 (and_2_out, en, str);
  EEPROMDualPort #(.AddrBits(3), .Bits(16)) \u_数据存储  (
    .A(D_out), .Din(S), .str(and_2_out), .C(C_t), .ld(ld), .D(\数据存储_d ));
  EEPROMDualPort #(.AddrBits(3), .Bits(16)) \u_指令存储  (
    .A(D_out), .Din(D0_in), .str(str0), .C(C_t), .ld(ld_0),
    .D({halt, \指令存储_d [14:13], ld, str, \指令存储_d [10:6], sel_B, \指令存储_d [3:0]}));
  Register #(.Bits(16)) register_1 (.D(_00_alu_01_1_s), .C(C_t), .en(en), .Q(S));
  Multiplexer #(.Bits(16), .Selector_Bits(2)) multiplexer_1 (
    .sel(sel_B), .in_0(\数据存储_d ), .in_1({16{1'b0}}), .in_2({16{1'b0}}), .in_3({16{1'b0}}),
    .out(multiplexer_1_out));
  _00_ALU_01 _00_alu_01_1 (.A(S), .B(multiplexer_1_out), .sel(\指令存储_d [1:0]), .S(_00_alu_01_1_s));  // open: C_out, ZF

  // Other names for the same wires on the sheet: D_in[15:0] = S

  // Notes on the sheet:
  //   contents of 数据存储 (hex, n*v repeats v):
  //   1e,28,32,3c,50
  //   contents of 指令存储 (hex, n*v repeats v):
  //   9000,9000,9001,9000,8810
endmodule
