// Digital circuit 00-ALU-10-组合cpu-编写ldA控制信号实现多次计算的重新加载.dig as structural Verilog
module \_00_ALU_10_组合cpu_编写ldA控制信号实现多次计算的重新加载  (
  input  en,
  input  C,
  input  [15:0] D0_in,
  input  str0,
  input  ld_0,
  output [15:0] S
);

  wire and_2_out, C_t, halt, ld, str;
  wire [1:0] sel_A, sel_B;
  wire [3:0] D_out;
  wire [14:0] \指令存储_d ;
  wire [15:0] multiplexer_1_out, multiplexer_2_out, \数据存储_d , \运算器_s ;

  and and_1 (C_t, C, halt);
  \_05_4位计数器  \_05_4位计数器_1  (.en(en), .C(C_t), .D_out(D_out));  // open: ovf
  and and_2 (and_2_out, en, str);
  Register #(.Bits(16)) \u_寄存器  (.D(\运算器_s ), .C(C_t), .en(en), .Q(S));
  EEPROMDualPort #(.AddrBits(4), .Bits(16)) \u_数据存储  (
    .A(D_out), .Din(S), .str(and_2_out), .C(C_t), .ld(ld), .D(\数据存储_d ));
  EEPROMDualPort #(.AddrBits(4), .Bits(16)) \u_指令存储  (
    .A(D_out), .Din(D0_in), .str(str0), .C(C_t), .ld(ld_0),
    .D({halt, \指令存储_d [14:13], ld, str, \指令存储_d [10:6], sel_B, sel_A, \指令存储_d [1:0]}));
  Multiplexer #(.Bits(16), .Selector_Bits(2)) multiplexer_1 (
    .sel(sel_A), .in_0(S), .in_1({16{1'b0}}), .in_2({16{1'b0}}), .in_3({16{1'b0}}), .out(multiplexer_1_out));
  Multiplexer #(.Selector_Bits(2), .Bits(16)) multiplexer_2 (
    .sel(sel_B), .in_0(\数据存储_d ), .in_1({16{1'b0}}), .in_2({16{1'b0}}), .in_3({16{1'b0}}),
    .out(multiplexer_2_out));
  _00_ALU_01 \u_运算器  (
    .A(multiplexer_1_out), .B(multiplexer_2_out), .sel(\指令存储_d [1:0]), .S(\运算器_s ));  // open: C_out, ZF

  // Other names for the same wires on the sheet: D_in[15:0] = S

  // Notes on the sheet:
  //   contents of 数据存储 (hex, n*v repeats v):
  //   1e,28,32,3c,50,1e,f,5,14
  //   contents of 指令存储 (hex, n*v repeats v):
  //   9004,9000,9001,9000,8810,9004,9001,9000,8810
endmodule
