// Digital circuit 00-ALU-11-组合cpu-编写jump指令完成跳转操作.dig as structural Verilog
module \_00_ALU_11_组合cpu_编写jump指令完成跳转操作  (
  input  en,
  input  C,
  input  [15:0] D0_in,
  input  str0,
  input  ld_0,
  output [15:0] S,
  output [3:0] c_2
);

  wire and_2_out, C_t, en_pc, halt, ld, ld_pc, str;
  wire [1:0] sel_A, sel_B;
  wire [3:0] addr;
  wire [14:0] \指令存储_d ;
  wire [15:0] multiplexer_1_out, \数据存储_d , \运算器_s ;
  wire [15:4] multiplexer_2_out;

  and and_1 (C_t, C, halt);
  and and_2 (and_2_out, en, str);
  \_05_4位计数器_带jump指令  \_05_4位计数器_带jump指令_1  (
    .en_pc(en_pc), .C(C_t), .ld_pc(ld_pc), .addr(addr), .D_out(c_2));  // open: ovf
  Register #(.Bits(16)) \u_寄存器  (.D(\运算器_s ), .C(C_t), .en(en), .Q(S));
  EEPROMDualPort #(.AddrBits(4), .Bits(16)) \u_数据存储  (
    .A(c_2), .Din(S), .str(and_2_out), .C(C_t), .ld(ld), .D(\数据存储_d ));
  EEPROMDualPort #(.AddrBits(4), .Bits(16)) \u_指令存储  (
    .A(c_2), .Din(D0_in), .str(str0), .C(C_t), .ld(ld_0),
    .D({halt, \指令存储_d [14:13], ld, str, ld_pc, \指令存储_d [9], en_pc, \指令存储_d [7:6], sel_B, sel_A, \指令存储_d [1:0]}));
  Multiplexer #(.Selector_Bits(2), .Bits(16)) multiplexer_1 (
    .sel(sel_A), .in_0(S), .in_1({16{1'b0}}), .in_2({16{1'b0}}), .in_3({16{1'b0}}), .out(multiplexer_1_out));
  Multiplexer #(.Selector_Bits(2), .Bits(16)) multiplexer_2 (
    .sel(sel_B), .in_0(\数据存储_d ), .in_1({16{1'b0}}), .in_2({16{1'b0}}), .in_3({16{1'b0}}),
    .out({multiplexer_2_out, addr}));
  _00_ALU_01 \u_运算器  (
    .A(multiplexer_1_out), .B({multiplexer_2_out, addr}), .sel(\指令存储_d [1:0]), .S(\运算器_s ));  // open: C_out, ZF

  // Other names for the same wires on the sheet: D_in[15:0] = S; D_out[3:0] = c_2

  // Notes on the sheet:
  //   en: default 1
  //   ld_0: default 1
  //   contents of 数据存储 (hex, n*v repeats v):
  //   5,28,32,3c,50,1e,f,5,28
  //   contents of 指令存储 (hex, n*v repeats v):
  //   9404,9000,9001,9000,8810,9104,9100,9101,8910
endmodule
