// Digital circuit 00-ALU-15-组合cpu-添加控制器使用控制编码对应指令.dig as structural Verilog
module \_00_ALU_15_组合cpu_添加控制器使用控制编码对应指令  (
  input  C,
  input  [15:0] D0_in,
  input  str0,
  input  ld_0,
  output [15:0] S,
  output [3:0] c_2,
  output c_3
);

  wire and_1_out, C_t, en_a, en_pc, halt, je_en, jmp_en, ld, or_1_out, str, ZF;
  wire [1:0] \_06_控制器_1_alu , sel_A, sel_B;
  wire [3:0] addr;
  wire [15:0] multiplexer_1_out, \指令存储_d , \数据存储_d , \运算器_s ;
  wire [15:4] multiplexer_2_out;

  and and_1 (and_1_out, c_3, je_en);
  or or_1 (or_1_out, and_1_out, jmp_en);
  and and_2 (C_t, C, halt);
  \_05_4位计数器_带jump指令  \_05_4位计数器_带jump指令_1  (
    .en_pc(en_pc), .C(C_t), .ld_pc(or_1_out), .addr(addr), .D_out(c_2));  // open: ovf
  Register \u_比较寄存器  (.D(ZF), .C(C_t), .en(en_a), .Q(c_3));
  Register #(.Bits(16)) \u_寄存器  (.D(\运算器_s ), .C(C_t), .en(en_a), .Q(S));
  EEPROMDualPort #(.AddrBits(4), .Bits(16)) \u_数据存储  (.A(c_2), .Din(S), .str(str), .C(C_t), .ld(ld), .D(\数据存储_d ));
  EEPROMDualPort #(.AddrBits(4), .Bits(16)) \u_指令存储  (
    .A(c_2), .Din(D0_in), .str(str0), .C(C_t), .ld(ld_0), .D(\指令存储_d ));
  \_06_控制器  \_06_控制器_1  (
    .opcode(\指令存储_d [15:11]), .alu(\_06_控制器_1_alu ), .sel_A(sel_A), .sel_B(sel_B), .en_a(en_a),
    .en_pc(en_pc), .je_en(je_en), .jmp_en(jmp_en), .str(str), .ld(ld), .halt(halt));
  Multiplexer #(.Selector_Bits(2), .Bits(16)) multiplexer_1 (
    .sel(sel_A), .in_0(S), .in_1({16{1'b0}}), .in_2({16{1'b0}}), .in_3({16{1'b0}}), .out(multiplexer_1_out));
  Multiplexer #(.Selector_Bits(2), .Bits(16)) multiplexer_2 (
    .sel(sel_B), .in_0(\数据存储_d ), .in_1({16{1'b0}}), .in_2({16{1'b0}}), .in_3({16{1'b0}}),
    .out({multiplexer_2_out, addr}));
  _00_ALU_01 \u_运算器  (
    .A(multiplexer_1_out), .B({multiplexer_2_out, addr}), .sel(\_06_控制器_1_alu ), .S(\运算器_s ), .ZF(ZF));  // open: C_out

  // Other names for the same wires on the sheet: D_in[15:0] = S; D_out[3:0] = c_2; Q_cmp = c_3

  // Notes on the sheet:
  //   ld_0: default 1
  //   contents of 数据存储 (hex, n*v repeats v):
  //   5,28,32,3c,50,c,2,5,f,5
  //   contents of 指令存储 (hex, n*v repeats v):
  //   3800,4*0,800,1800,1000,1000,4000
endmodule
