// Digital circuit 00-ALU-16-组合cpu-合并内存之后完整的计算单元.dig as structural Verilog
module \_00_ALU_16_组合cpu_合并内存之后完整的计算单元  (
  input  C,
  output [15:0] out,
  output [10:0] c_2,
  output c_3,
  output [15:0] D_out,
  output [4:0] opcode,
  output Q_cmp,
  output [10:0] A
);

  wire button_1_out, C_t, en_a, en_addr, en_cmp, en_pc, halt, ld, ld_pc, str, ZF;
  wire [1:0] \_06_控制器_2_1_alu , sel_A, sel_B;
  wire [10:0] addr;
  wire [15:0] multiplexer_2_out, multiplexer_3_out, \运算器_s ;

  and and_1 (C_t, button_1_out, halt);
  Button button_1 (.out(button_1_out));
  // _05_变量_计数器 #(.generic("Bits := 11;")) 计数器: pin names not known; wires that end beside it: C, en_pc, C_t, ld_pc, addr, c_2
  Multiplexer #(.Bits(11)) multiplexer_1 (.sel(en_pc), .in_0(addr), .in_1(c_2), .out(A));
  Register #(.Bits(16)) \u_指令寄存器  (.D(D_out), .C(C_t), .en(en_addr), .Q({opcode, addr}));
  Register \u_比较寄存器  (.D(ZF), .C(C_t), .en(en_cmp), .Q(c_3));
  Register #(.Bits(16)) \u_寄存器  (.D(\运算器_s ), .C(C_t), .en(en_a), .Q(out));
  EEPROMDualPort #(.AddrBits(11), .Bits(16)) \u_内存RAM  (.A(A), .Din(out), .str(str), .C(C_t), .ld(ld), .D(D_out));
  \_06_控制器_2  \_06_控制器_2_1  (
    .opcode(opcode), .cmp(c_3), .clock(C_t), .alu(\_06_控制器_2_1_alu ), .sel_A(sel_A), .sel_B(sel_B),
    .en_a(en_a), .en_pc(en_pc), .en_cmp(en_cmp), .ld_pc(ld_pc), .str(str), .ld(ld), .halt(halt),
    .en_addr(en_addr));
  Multiplexer #(.Selector_Bits(2), .Bits(16)) multiplexer_2 (
    .sel(sel_A), .in_0(out), .in_1({16{1'b0}}), .in_2({16{1'b0}}), .in_3({16{1'b0}}), .out(multiplexer_2_out));
  Multiplexer #(.Selector_Bits(2), .Bits(16)) multiplexer_3 (
    .sel(sel_B), .in_0(D_out), .in_1({16{1'b0}}), .in_2({16{1'b0}}), .in_3({16{1'b0}}),
    .out(multiplexer_3_out));
  _00_ALU_01 \u_运算器  (
    .A(multiplexer_2_out), .B(multiplexer_3_out), .sel(\_06_控制器_2_1_alu ), .S(\运算器_s ), .ZF(ZF));  // open: C_out

  assign Q_cmp = c_3;

  // Other names for the same wires on the sheet: D_in[15:0] = out; pc_addr[10:0] = c_2

  // Notes on the sheet:
  //   contents of 内存RAM (hex, n*v repeats v):
  //   808,1009,180a,300b,4*0,a,f,5,14
endmodule
