// Digital circuit 00-ALU-18-组合cpu-两个寄存器的完整电路.dig as structural Verilog
module \_00_ALU_18_组合cpu_两个寄存器的完整电路  (
  input  C,
  output [15:0] S_b,
  output [10:0] c_2,
  output c_3,
  output [15:0] D_out,
  output [4:0] opcode,
  output Q_cmp,
  output [10:0] A,
  output [15:0] S_a,
  output [15:0] S_alu_a,
  output [15:0] S_alu_b
);

  wire button_1_out, C_t, en_a, en_addr, en_b, en_cmp, en_i, en_pc, halt, ld, ld_pc, str, ZF;
  wire [1:0] \_06_控制器_4_添加b寄存器_1_alu , sel_A, sel_B;
  wire [10:0] addr;
  wire [15:0] S;

  and and_1 (C_t, button_1_out, halt);
  Button button_1 (.out(button_1_out));
  // _05_变量_计数器 #(.generic("Bits := 11;")) 计数器: pin names not known; wires that end beside it: C, en_pc, C_t, ld_pc, addr, c_2
  Multiplexer #(.Bits(11)) multiplexer_1 (.sel(en_pc), .in_0(addr), .in_1(c_2), .out(A));
  Register #(.Bits(16)) \u_指令寄存器  (.D(D_out), .C(C_t), .en(en_addr), .Q({opcode, addr}));
  Register \u_比较寄存器  (.D(ZF), .C(C_t), .en(en_cmp), .Q(c_3));
  assign D_out = en_i ? {{5{1'b0}}, addr} : 16'bz;  // Driver driver_1
  Register #(.Bits(16)) \u_寄存器A  (.D(S), .C(C_t), .en(en_a), .Q(S_a));
  Register #(.Bits(16)) \u_寄存器B  (.D(S), .C(C_t), .en(en_b), .Q(S_b));
  EEPROMDualPort #(.AddrBits(11), .Bits(16)) \u_内存RAM  (.A(A), .Din(S), .str(str), .C(C_t), .ld(ld), .D(D_out));
  \_06_控制器_4_添加b寄存器  \_06_控制器_4_添加b寄存器_1  (
    .opcode(opcode), .cmp(c_3), .clock(C_t), .alu(\_06_控制器_4_添加b寄存器_1_alu ), .sel_A(sel_A), .sel_B(sel_B),
    .en_a(en_a), .en_b(en_b), .en_pc(en_pc), .en_cmp(en_cmp), .ld_pc(ld_pc), .str(str), .ld(ld), .halt(halt),
    .en_addr(en_addr), .en_i(en_i));
  Multiplexer #(.Selector_Bits(2), .Bits(16)) multiplexer_2 (
    .sel(sel_A), .in_0(S_a), .in_1(S_b), .in_2({16{1'b0}}), .in_3(D_out), .out(S_alu_a));
  Multiplexer #(.Selector_Bits(2), .Bits(16)) multiplexer_3 (
    .sel(sel_B), .in_0(S_a), .in_1(S_b), .in_2({16{1'b0}}), .in_3(D_out), .out(S_alu_b));
  _00_ALU_01 \u_运算器  (.A(S_alu_a), .B(S_alu_b), .sel(\_06_控制器_4_添加b寄存器_1_alu ), .S(S), .ZF(ZF));  // open: C_out

  assign Q_cmp = c_3;

  // Other names for the same wires on the sheet: alu_A[15:0] = S_alu_a; alu_B[15:0] = S_alu_b; pc_addr[10:0] = c_2;
  //   Q_a[15:0] = S_a; Q_b[15:0] = S_b

  // Notes on the sheet:
  //   C: Hz: 50
  //   contents of 内存RAM (hex, n*v repeats v):
  //   4800,5001,a805,2800,6001,a065,b803,1810,8*0,13ba
endmodule
