// Digital circuit 00-CPU-01.dig as structural Verilog
module _00_CPU_01 (
  input  C,
  input  [15:0] D_in,
  output [10:0] A,
  output ld,
  output str,
  output [15:0] D_out
);

  wire and_2_out, and_3_out, C_t, en_a, en_addr, en_b, en_cmp, en_i, en_irom, en_pc, halt, ld_pc, Q_cmp, ZF;
  wire [1:0] \_06_控制器_4_添加b寄存器_1_alu , sel_A, sel_B;
  wire [4:0] opcode;
  wire [10:0] addr, pc_addr;
  wire [15:0] alu_A, alu_B, Q_a, Q_b;

  Register #(.Bits(16)) \u_指令寄存器  (.D(D_in), .C(C_t), .en(en_addr), .Q({opcode, addr}));
  and and_1 (C_t, C, halt);
  // _05_变量_计数器 #(.generic("Bits := 11;")) 计数器: pin names not known; wires that end beside it: en_pc, C_t, ld_pc, addr, pc_addr
  Register \u_比较寄存器  (.D(ZF), .C(C_t), .en(en_cmp), .Q(Q_cmp));
  Multiplexer #(.Bits(11)) multiplexer_1 (.sel(en_pc), .in_0(addr), .in_1(pc_addr), .out(A));
  nor nor_1 (en_irom, A[8], A[9], A[10]);
  Register #(.Bits(16)) \u_寄存器A  (.D(D_out), .C(C_t), .en(en_a), .Q(Q_a));
  Register #(.Bits(16)) \u_寄存器B  (.D(D_out), .C(C_t), .en(en_b), .Q(Q_b));
  assign D_in = en_i ? {{5{1'b0}}, addr} : 16'bz;  // Driver driver_1
  \_06_控制器_4_添加b寄存器  \_06_控制器_4_添加b寄存器_1  (
    .opcode(opcode), .cmp(Q_cmp), .clock(C_t), .alu(\_06_控制器_4_添加b寄存器_1_alu ), .sel_A(sel_A), .sel_B(sel_B),
    .en_a(en_a), .en_b(en_b), .en_pc(en_pc), .en_cmp(en_cmp), .ld_pc(ld_pc), .str(str), .ld(ld), .halt(halt),
    .en_addr(en_addr), .en_i(en_i));
  and and_2 (and_2_out, str, en_irom);
  and and_3 (and_3_out, ld, en_irom);
  Multiplexer #(.Selector_Bits(2), .Bits(16)) multiplexer_2 (
    .sel(sel_A), .in_0(Q_a), .in_1(Q_b), .in_2({16{1'b0}}), .in_3(D_in), .out(alu_A));
  Multiplexer #(.Selector_Bits(2), .Bits(16)) multiplexer_3 (
    .sel(sel_B), .in_0(Q_a), .in_1(Q_b), .in_2({16{1'b0}}), .in_3(D_in), .out(alu_B));
  _00_ALU_01 \u_运算器  (.A(alu_A), .B(alu_B), .sel(\_06_控制器_4_添加b寄存器_1_alu ), .S(D_out), .ZF(ZF));  // open: C_out
  EEPROMDualPort #(.AddrBits(8), .Bits(16)) \u_内存RAM  (
    .A(A[7:0]), .Din(D_out), .str(and_2_out), .C(C_t), .ld(and_3_out), .D(D_in));

  // Other names for the same wires on the sheet: addr_irom[7:0] = A[7:0]; S[15:0] = D_out

  // Notes on the sheet:
  //   C: Hz: 50
  //   contents of 内存RAM (hex, n*v repeats v):
  //   5000,810,19ff,80e,2800,19fd,80f,2800,19fe,a9fd,6001,a020,b803
  //   ,a900,a00,1900,a80a
endmodule
