// Digital circuit 00-计算机-01.dig as structural Verilog
module \_00_计算机_01  (
  input  clk
);

  wire and_1_out, and_2_out, and_4_out, and_5_out, and_6_out, en_ram, en_rom, ld, not_1_out, not_2_out,
       not_3_out, not_4_out, not_5_out, not_6_out, not_7_out, not_8_out, not_9_out, not_10_out, not_11_out,
       not_12_out, not_13_out, str;
  wire [10:0] A;
  wire [15:0] D_in, D_out;

  and and_1 (and_1_out, str, en_ram);
  and and_2 (and_2_out, ld, en_ram);
  _00_CPU_01 _00_cpu_01_1 (.C(clk), .D_in(D_in), .A(A), .ld(ld), .str(str), .D_out(D_out));
  and and_3 (en_ram, A[8], not_1_out, not_2_out);
  not not_1 (not_1_out, A[9]);
  not not_2 (not_2_out, A[10]);
  RAMDualPort #(.AddrBits(8), .Bits(16)) ramdualport_1 (
    .A(A[7:0]), .Din(D_out), .str(and_1_out), .C(clk), .ld(and_2_out), .D(D_in));
  not not_3 (not_3_out, A[0]);
  not not_4 (not_4_out, A[1]);
  not not_5 (not_5_out, A[2]);
  not not_6 (not_6_out, A[3]);
  not not_7 (not_7_out, A[4]);
  not not_8 (not_8_out, A[5]);
  not not_9 (not_9_out, A[6]);
  not not_10 (not_10_out, A[7]);
  not not_11 (not_11_out, A[10]);
  and and_4 (and_4_out, str, en_rom);
  and and_5 (and_5_out, ld, en_rom);
  and and_6 (and_6_out, not_3_out, not_4_out, not_5_out, not_6_out, not_7_out, not_8_out, not_9_out, not_10_out, A[8], A[9], not_11_out);
  and and_7 (en_rom, not_12_out, A[9], not_13_out);
  not not_12 (not_12_out, A[8]);
  not not_13 (not_13_out, A[10]);
  Terminal terminal_1 (.D(D_out[7:0]), .C(clk), .en(and_6_out));
  EEPROMDualPort #(.AddrBits(8), .Bits(16)) eepromdualport_1 (
    .A(A[7:0]), .Din(D_out), .str(and_4_out), .C(clk), .ld(and_5_out), .D(D_in));

  // Other names for the same wires on the sheet: addr_ram[7:0] = A[7:0]; addr_rom[7:0] = A[7:0]; clock = clk

  // Notes on the sheet:
  //   clk: Hz: 500
  //   contents of eepromdualport_1 (hex, n*v repeats v):
  //   5000,910,19ff,90e,2800,19fd,90f,2800,19fe,a9fd,6001,a019,b903
  //   ,a920,a20,1920,a90a,15*0,4848,1b00,4865,1b00,486c,1b00,486c,1b00
  //   ,486f,1b00,4820,1b00,4877,1b00,486f,1b00,4872,1b00,486c,1b00,4864
  //   ,1b00,4821,1b00
endmodule
