// Digital circuit 01-1位复用器.dig as structural Verilog
module \_01_1位复用器  (
  input  S1,
  input  S2,
  input  sel,
  output S
);

  // RelayDT relaydt_1: pin names not known; wires that end beside it: sel, S2, S1, 1'b0, S
endmodule
