// Digital circuit 01-2位复用器.dig as structural Verilog
module \_01_2位复用器  (
  input  [1:0] sel,
  input  in_2,
  input  in_3,
  input  in_4,
  input  in_5,
  output S
);

  wire \_01_1位复用器_1_s , \_01_1位复用器_2_s ;

  \_01_1位复用器  \_01_1位复用器_1  (.S1(in_2), .S2(in_3), .sel(sel[0]), .S(\_01_1位复用器_1_s ));
  \_01_1位复用器  \_01_1位复用器_2  (.S1(in_4), .S2(in_5), .sel(sel[0]), .S(\_01_1位复用器_2_s ));
  \_01_1位复用器  \_01_1位复用器_3  (.S1(\_01_1位复用器_1_s ), .S2(\_01_1位复用器_2_s ), .sel(sel[1]), .S(S));
endmodule
