// Digital circuit 02-2位比较器.dig as structural Verilog
module \_02_2位比较器  (
  input  [1:0] A,
  input  [1:0] B,
  output S
);

  wire \_02_1位比较器_1_x , \_02_1位比较器_2_x ;

  \_02_1位比较器  \_02_1位比较器_1  (.A(A[0]), .B(B[0]), .X(\_02_1位比较器_1_x ));
  \_02_1位比较器  \_02_1位比较器_2  (.A(A[1]), .B(B[1]), .X(\_02_1位比较器_2_x ));
  and and_1 (S, \_02_1位比较器_1_x , \_02_1位比较器_2_x );
endmodule
