// Digital circuit 03-3-8译码器.dig as structural Verilog
module \_03_3_8译码器  (
  input  C,
  input  B,
  input  A,
  output S_0,
  output S_1,
  output S_2,
  output S_3,
  output S_4,
  output S_5,
  output S_6,
  output S_7
);

  wire not_1_out, not_2_out, not_3_out;

  not not_1 (not_1_out, A);
  not not_2 (not_2_out, B);
  not not_3 (not_3_out, C);
  and and_1 (S_0, not_1_out, not_2_out, not_3_out);
  and and_2 (S_1, not_1_out, not_2_out, C);
  and and_3 (S_2, not_1_out, B, not_3_out);
  and and_4 (S_3, not_1_out, B, C);
  and and_5 (S_4, A, not_2_out, not_3_out);
  and and_6 (S_5, A, not_2_out, C);
  and and_7 (S_6, A, B, not_3_out);
  and and_8 (S_7, A, B, C);
endmodule
