// Digital circuit 04-简易内存-01.dig as structural Verilog
module \_04_简易内存_01  (
  input  [2:0] Addr,
  input  [15:0] D,
  input  C,
  output [15:0] out_4,
  output [15:0] out_5,
  output [15:0] out_6,
  output [15:0] out_7,
  output [15:0] out_8,
  output [15:0] out_9,
  output [15:0] out_10,
  output [15:0] out_11
);

  wire s_0, s_1, s_2, s_3, s_4, s_5, s_6, s_7;

  \_03_3_8译码器  \_03_3_8译码器_1  (
    .C(Addr[0]), .B(Addr[1]), .A(Addr[2]), .S_0(s_0), .S_1(s_1), .S_2(s_2), .S_3(s_3), .S_4(s_4), .S_5(s_5),
    .S_6(s_6), .S_7(s_7));
  Register #(.Bits(16)) register_1 (.D(D), .C(C), .en(s_0), .Q(out_4));
  Register #(.Bits(16)) register_2 (.D(D), .C(C), .en(s_2), .Q(out_6));
  Register #(.Bits(16)) register_3 (.D(D), .C(C), .en(s_4), .Q(out_8));
  Register #(.Bits(16)) register_4 (.D(D), .C(C), .en(s_6), .Q(out_10));
  Register #(.Bits(16)) register_5 (.D(D), .C(C), .en(s_1), .Q(out_5));
  Register #(.Bits(16)) register_6 (.D(D), .C(C), .en(s_3), .Q(out_7));
  Register #(.Bits(16)) register_7 (.D(D), .C(C), .en(s_5), .Q(out_9));
  Register #(.Bits(16)) register_8 (.D(D), .C(C), .en(s_7), .Q(out_11));

  // Other names for the same wires on the sheet: c_0 = C; D_0[15:0] = D
endmodule
