// Digital circuit 04-简易内存-02-EEPROM.dig as structural Verilog
module \_04_简易内存_02_EEPROM  (
  input  [2:0] Addr,
  input  [15:0] D,
  input  C,
  input  str,
  input  ld,
  output [15:0] D_out
);

  wire c_0, s_0, s_1, s_2, s_3, s_4, s_5, s_6, s_7;
  wire [15:0] multiplexer_1_out, q_0, q_1, q_2, q_3, q_4, q_5, q_6, q_7;

  and and_1 (c_0, C, str);
  \_03_3_8译码器  \_03_3_8译码器_1  (
    .C(Addr[0]), .B(Addr[1]), .A(Addr[2]), .S_0(s_0), .S_1(s_1), .S_2(s_2), .S_3(s_3), .S_4(s_4), .S_5(s_5),
    .S_6(s_6), .S_7(s_7));
  Register #(.Bits(16)) register_1 (.D(D), .C(c_0), .en(s_0), .Q(q_0));
  Register #(.Bits(16)) register_2 (.D(D), .C(c_0), .en(s_2), .Q(q_2));
  Register #(.Bits(16)) register_3 (.D(D), .C(c_0), .en(s_4), .Q(q_4));
  Register #(.Bits(16)) register_4 (.D(D), .C(c_0), .en(s_6), .Q(q_6));
  Register #(.Bits(16)) register_5 (.D(D), .C(c_0), .en(s_1), .Q(q_1));
  Register #(.Bits(16)) register_6 (.D(D), .C(c_0), .en(s_3), .Q(q_3));
  Register #(.Bits(16)) register_7 (.D(D), .C(c_0), .en(s_5), .Q(q_5));
  Register #(.Bits(16)) register_8 (.D(D), .C(c_0), .en(s_7), .Q(q_7));
  Multiplexer #(.Bits(16), .Selector_Bits(3)) multiplexer_1 (
    .sel(Addr), .in_0(q_0), .in_1(q_1), .in_2(q_2), .in_3(q_3), .in_4(q_4), .in_5(q_5), .in_6(q_6),
    .in_7(q_7), .out(multiplexer_1_out));
  assign D_out = ld ? multiplexer_1_out : 16'bz;  // Driver driver_1

  // Other names for the same wires on the sheet: D_0[15:0] = D
endmodule
