// Digital circuit 05-2位计数器.dig as structural Verilog
module \_05_2位计数器  (
  input  en,
  input  C,
  output ovf,
  output [1:0] D_out
);

  wire [1:0] add_1_s;

  Register #(.Bits(2)) register_1 (.D(add_1_s), .C(C), .en(en), .Q(D_out));
  Add #(.Bits(2)) add_1 (.a(D_out), .b(2'b01), .c_i(1'b0), .s(add_1_s), .c_o(ovf));
endmodule
