// Digital circuit 05-3位计数器.dig as structural Verilog
module \_05_3位计数器  (
  input  en,
  input  C,
  output ovf,
  output [2:0] D_out
);

  wire [2:0] add_1_s;

  Register #(.Bits(3)) register_1 (.D(add_1_s), .C(C), .en(en), .Q(D_out));
  Add #(.Bits(3)) add_1 (.a(D_out), .b(3'b001), .c_i(1'b0), .s(add_1_s), .c_o(ovf));
endmodule
