// Digital circuit 05-4位计数器-带jump指令.dig as structural Verilog
module \_05_4位计数器_带jump指令  (
  input  en_pc,
  input  C,
  input  ld_pc,
  input  [3:0] addr,
  output ovf,
  output [3:0] D_out
);

  wire or_1_out;
  wire [3:0] add_1_s, multiplexer_1_out;

  or or_1 (or_1_out, ld_pc, en_pc);
  Multiplexer #(.Bits(4)) multiplexer_1 (.sel(ld_pc), .in_0(add_1_s), .in_1(addr), .out(multiplexer_1_out));
  Register #(.Bits(4)) register_1 (.D(multiplexer_1_out), .C(C), .en(or_1_out), .Q(D_out));
  Add #(.Bits(4)) add_1 (.a(D_out), .b(4'b0001), .c_i(1'b0), .s(add_1_s), .c_o(ovf));
endmodule
