// Digital circuit 05-4位计数器.dig as structural Verilog
module \_05_4位计数器  (
  input  en,
  input  C,
  output ovf,
  output [3:0] D_out
);

  wire [3:0] add_1_s;

  Register #(.Bits(4)) register_1 (.D(add_1_s), .C(C), .en(en), .Q(D_out));
  Add #(.Bits(4)) add_1 (.a(D_out), .b(4'b0001), .c_i(1'b0), .s(add_1_s), .c_o(ovf));
endmodule
