// Digital circuit 06-控制器-2.dig as structural Verilog
module \_06_控制器_2  (
  input  [4:0] opcode,
  input  cmp,
  input  clock,
  output [1:0] alu,
  output [1:0] sel_A,
  output [1:0] sel_B,
  output en_a,
  output en_pc,
  output en_cmp,
  output ld_pc,
  output str,
  output ld,
  output halt,
  output en_addr
);

  wire d_ff_1_nq, d_ff_1_q;
  wire [14:7] lookuptable_1_out;

  D_FF d_ff_1 (.D(d_ff_1_nq), .C(clock), .Q(d_ff_1_q), .nQ(d_ff_1_nq));
  LookUpTable #(.Bits(16)) lookuptable_1 (
    .in0(opcode[0]), .in1(opcode[1]), .in2(opcode[2]), .in3(opcode[3]), .in4(opcode[4]), .in5(cmp),
    .in6(d_ff_1_q),
    .out({halt, lookuptable_1_out[14], en_addr, ld, str, ld_pc, en_cmp, en_pc, lookuptable_1_out[7], en_a, sel_B, sel_A, alu}));

  // Notes on the sheet:
  //   contents of lookuptable_1 (hex, n*v repeats v):
  //   9*b100,23*0,9*b100,24*0,9044,9040,9041,9043,9042,9810,8400,8000
  //   ,24*0,9044,9040,9041,9043,9042,9810,8400,8400
endmodule
