// Digital circuit 06-控制器-3-添加立即数.dig as structural Verilog
module \_06_控制器_3_添加立即数  (
  input  [4:0] opcode,
  input  cmp,
  input  clock,
  output [1:0] alu,
  output [1:0] sel_A,
  output [1:0] sel_B,
  output en_a,
  output en_pc,
  output en_cmp,
  output ld_pc,
  output str,
  output ld,
  output halt,
  output en_addr,
  output en_i
);

  wire d_ff_1_nq, d_ff_1_q;
  wire [7:7] lookuptable_1_out;

  D_FF d_ff_1 (.D(d_ff_1_nq), .C(clock), .Q(d_ff_1_q), .nQ(d_ff_1_nq));
  LookUpTable #(.Bits(16)) lookuptable_1 (
    .in0(opcode[0]), .in1(opcode[1]), .in2(opcode[2]), .in3(opcode[3]), .in4(opcode[4]), .in5(cmp),
    .in6(d_ff_1_q),
    .out({halt, en_i, en_addr, ld, str, ld_pc, en_cmp, en_pc, lookuptable_1_out[7], en_a, sel_B, sel_A, alu}));

  // Notes on the sheet:
  //   contents of lookuptable_1 (hex, n*v repeats v):
  //   14*b100,18*0,14*b100,19*0,9044,9040,9041,9043,9042,9810,8400,8000
  //   ,c074,c070,c071,c073,c072,19*0,9044,9040,9041,9043,9042,9810,8400
  //   ,8000,c074,c070,c071,c073,c072
endmodule
