// Digital circuit 06-控制器-4-添加b寄存器.dig as structural Verilog
module \_06_控制器_4_添加b寄存器  (
  input  [4:0] opcode,
  input  cmp,
  input  clock,
  output [1:0] alu,
  output [1:0] sel_A,
  output [1:0] sel_B,
  output en_a,
  output en_b,
  output en_pc,
  output en_cmp,
  output ld_pc,
  output str,
  output ld,
  output halt,
  output en_addr,
  output en_i
);

  wire d_ff_1_nq, d_ff_1_q;

  D_FF d_ff_1 (.D(d_ff_1_nq), .C(clock), .Q(d_ff_1_q), .nQ(d_ff_1_nq));
  LookUpTable #(.Bits(16)) lookuptable_1 (
    .in0(opcode[0]), .in1(opcode[1]), .in2(opcode[2]), .in3(opcode[3]), .in4(opcode[4]), .in5(cmp),
    .in6(d_ff_1_q), .out({halt, en_i, en_addr, ld, str, ld_pc, en_cmp, en_pc, en_b, en_a, sel_B, sel_A, alu}));

  // Notes on the sheet:
  //   contents of lookuptable_1 (hex, n*v repeats v):
  //   64*b100,0,9078,90b8,8820,8824,8050,80510,8052,8053,c078,c0b8,c070
  //   ,c0b4,c071,c0b5,c072,c0b6,c073,c0b7,230,c234,8400,8000,8400,8000
  //   ,8*0,9078,90b8,8820,8824,8050,510,8052,8053,c078,c0b8,c070,c0b4
  //   ,c071,c0b5,c072,c0b6,c073,c0b7,230,c234,8400,8400,8000,8000
endmodule
