// Digital circuit 06-控制器.dig as structural Verilog
module \_06_控制器  (
  input  [4:0] opcode,
  output [1:0] alu,
  output [1:0] sel_A,
  output [1:0] sel_B,
  output en_a,
  output en_pc,
  output je_en,
  output jmp_en,
  output str,
  output ld,
  output halt
);

  wire [14:7] lookuptable_1_out;

  LookUpTable #(.Bits(16)) lookuptable_1 (
    .in0(opcode[0]), .in1(opcode[1]), .in2(opcode[2]), .in3(opcode[3]), .in4(opcode[4]),
    .out({halt, lookuptable_1_out[14:13], ld, str, jmp_en, je_en, en_pc, lookuptable_1_out[7], en_a, sel_B, sel_A, alu}));

  // Notes on the sheet:
  //   contents of lookuptable_1 (hex, n*v repeats v):
  //   0,9144,9140,9141,9142,9143,8950,9404,9204
endmodule
