// Digital circuit test-10-加法器.dig as structural Verilog
module \test_10_加法器  (
  input  A,
  input  B,
  input  C_in,
  output S,
  output C_out
);

  wire \test_9_半加器_1_c , \test_9_半加器_1_s , \test_9_半加器_2_c ;

  \test_9_半加器  \test_9_半加器_1  (.A(A), .B(B), .S(\test_9_半加器_1_s ), .C(\test_9_半加器_1_c ));
  \test_9_半加器  \test_9_半加器_2  (.A(C_in), .B(\test_9_半加器_1_s ), .S(S), .C(\test_9_半加器_2_c ));
  or or_1 (C_out, \test_9_半加器_2_c , \test_9_半加器_1_c );
endmodule
