// Digital circuit test-11-4位加法器.dig as structural Verilog
module \test_11_4位加法器  (
  input  [3:0] A,
  input  [3:0] B,
  output [3:0] S,
  output C_out
);

  wire \test_10_加法器_1_c_out , \test_10_加法器_2_c_out , \test_10_加法器_3_c_out ;

  \test_10_加法器  \test_10_加法器_1  (.A(A[0]), .B(B[0]), .C_in(1'b0), .S(S[0]), .C_out(\test_10_加法器_1_c_out ));
  \test_10_加法器  \test_10_加法器_2  (
    .A(A[1]), .B(B[1]), .C_in(\test_10_加法器_1_c_out ), .S(S[1]), .C_out(\test_10_加法器_2_c_out ));
  \test_10_加法器  \test_10_加法器_3  (
    .A(A[2]), .B(B[2]), .C_in(\test_10_加法器_2_c_out ), .S(S[2]), .C_out(\test_10_加法器_3_c_out ));
  \test_10_加法器  \test_10_加法器_4  (.A(A[3]), .B(B[3]), .C_in(\test_10_加法器_3_c_out ), .S(S[3]), .C_out(C_out));

  // Notes on the sheet:
  //   A: default 8
  //   B: default 6
endmodule
