// Digital circuit test-12-半减器.dig as structural Verilog
module \test_12_半减器  (
  input  A,
  input  B,
  output S,
  output C
);

  wire and_1_out, and_2_out, not_1_out, not_2_out;

  not not_1 (not_1_out, A);
  not not_2 (not_2_out, B);
  and and_1 (and_1_out, not_1_out, B);
  and and_2 (and_2_out, A, not_2_out);
  and and_3 (C, not_1_out, B);
  or or_1 (S, and_1_out, and_2_out);
endmodule
