// Digital circuit test-13-4位减法器.dig as structural Verilog
module \test_13_4位减法器  (
  input  [3:0] A,
  input  [3:0] B,
  input  C_in,
  output [3:0] S,
  output C_out
);

  wire \test_13_减法器_1_c_out , \test_13_减法器_2_c_out , \test_13_减法器_3_c_out ;

  \test_13_减法器  \test_13_减法器_1  (.A(A[0]), .B(B[0]), .C_in(C_in), .S(S[0]), .C_out(\test_13_减法器_1_c_out ));
  \test_13_减法器  \test_13_减法器_2  (
    .A(A[2]), .B(B[2]), .C_in(\test_13_减法器_3_c_out ), .S(S[2]), .C_out(\test_13_减法器_2_c_out ));
  \test_13_减法器  \test_13_减法器_3  (
    .A(A[1]), .B(B[1]), .C_in(\test_13_减法器_1_c_out ), .S(S[1]), .C_out(\test_13_减法器_3_c_out ));
  \test_13_减法器  \test_13_减法器_4  (.A(A[3]), .B(B[3]), .C_in(\test_13_减法器_2_c_out ), .S(S[3]), .C_out(C_out));

  // Notes on the sheet:
  //   A: default 15
  //   B: default 3
endmodule
