// Digital circuit test-13-减法器.dig as structural Verilog
module \test_13_减法器  (
  input  A,
  input  B,
  input  C_in,
  output S,
  output C_out
);

  wire \test_12_半减器_1_c , \test_12_半减器_1_s , \test_12_半减器_2_c ;

  \test_12_半减器  \test_12_半减器_1  (.A(A), .B(B), .S(\test_12_半减器_1_s ), .C(\test_12_半减器_1_c ));
  \test_12_半减器  \test_12_半减器_2  (.A(\test_12_半减器_1_s ), .B(C_in), .S(S), .C(\test_12_半减器_2_c ));
  or or_1 (C_out, \test_12_半减器_2_c , \test_12_半减器_1_c );
endmodule
