// Digital circuit test-15-与非门-SR锁存器.dig as structural Verilog
module \test_15_与非门_SR锁存器  (
  input  S,
  input  R,
  output Q,
  output Q_2
);

  nand nand_1 (Q, S, Q_2);
  nand nand_2 (Q_2, Q, R);
endmodule
