// Digital circuit test-16-或非门-SR锁存器.dig as structural Verilog
module \test_16_或非门_SR锁存器  (
  input  S,
  input  R,
  output Q,
  output Q_2
);

  nor nor_1 (Q, S, Q_2);
  nor nor_2 (Q_2, Q, R);
endmodule
