// Digital circuit test-17-带en-或非门-SR锁存器.dig as structural Verilog
module \test_17_带en_或非门_SR锁存器  (
  input  S,
  input  en,
  input  R,
  output Q,
  output Q_2
);

  wire nand_1_out, nand_2_out;

  nand nand_1 (nand_1_out, S, en);
  nand nand_2 (nand_2_out, en, R);
  \test_15_与非门_SR锁存器  \test_15_与非门_sr锁存器_1  (.S(nand_1_out), .R(nand_2_out), .Q(Q), .Q_2(Q_2));
endmodule
