// Digital circuit test-18-带en-或非门-D锁存器.dig as structural Verilog
module \test_18_带en_或非门_D锁存器  (
  input  D,
  input  en,
  output Q,
  output Q_2
);

  wire nand_1_out, nand_2_out, not_1_out;

  not not_1 (not_1_out, D);
  nand nand_1 (nand_1_out, D, en);
  nand nand_2 (nand_2_out, en, not_1_out);
  \test_15_与非门_SR锁存器  \test_15_与非门_sr锁存器_1  (.S(nand_1_out), .R(nand_2_out), .Q(Q), .Q_2(Q_2));
endmodule
