// Digital circuit test-19-D触发器.dig as structural Verilog
module \test_19_D触发器  (
  input  D,
  input  en,
  output Q,
  output Q_2
);

  wire not_1_out, \test_18_带en_或非门_d锁存器_1_q ;

  \test_18_带en_或非门_D锁存器  \test_18_带en_或非门_d锁存器_1  (.D(D), .en(not_1_out), .Q(\test_18_带en_或非门_d锁存器_1_q ));  // open: Q_2
  not not_1 (not_1_out, en);
  \test_18_带en_或非门_D锁存器  \test_18_带en_或非门_d锁存器_2  (.D(\test_18_带en_或非门_d锁存器_1_q ), .en(en), .Q(Q), .Q_2(Q_2));
endmodule
