// Digital circuit test-2-feimen.dig as structural Verilog
module test_2_feimen (
  input  A,
  output B
);

  // Relay #(.relayNormallyClosed("true")) relay_1: pin names not known; wires that end beside it: A, 1'b1, 1'b0, B
  PullDown pulldown_1 (.out(B));
endmodule
