// Digital circuit test-20-4位时钟-D触发器.dig as structural Verilog
module \test_20_4位时钟_D触发器  (
  input  [3:0] D,
  input  C,
  output out_2,
  output out_3,
  output out_4,
  output out_5
);

  \test_19_D触发器  \test_19_d触发器_1  (.D(D[0]), .en(C), .Q(out_2));  // open: Q_2
  \test_19_D触发器  \test_19_d触发器_2  (.D(D[2]), .en(C), .Q(out_4));  // open: Q_2
  \test_19_D触发器  \test_19_d触发器_3  (.D(D[1]), .en(C), .Q(out_3));  // open: Q_2
  \test_19_D触发器  \test_19_d触发器_4  (.D(D[3]), .en(C), .Q(out_5));  // open: Q_2

  // Other names for the same wires on the sheet: c0 = C
endmodule
