// Digital circuit test-21-4位时钟-标准-D触发器.dig as structural Verilog
module \test_21_4位时钟_标准_D触发器  (
  input  [3:0] D,
  input  C,
  input  in_7,
  output s_0,
  output s_1,
  output s_2,
  output s_3
);

  wire c0;

  and and_1 (c0, C, in_7);
  \test_19_D触发器  \test_19_d触发器_1  (.D(D[0]), .en(c0), .Q(s_0));  // open: Q_2
  \test_19_D触发器  \test_19_d触发器_2  (.D(D[2]), .en(c0), .Q(s_2));  // open: Q_2
  \test_19_D触发器  \test_19_d触发器_3  (.D(D[1]), .en(c0), .Q(s_1));  // open: Q_2
  \test_19_D触发器  \test_19_d触发器_4  (.D(D[3]), .en(c0), .Q(s_3));  // open: Q_2
endmodule
