// Digital circuit test-22-带寄存器的加法器.dig as structural Verilog
module \test_22_带寄存器的加法器  (
  input  [15:0] B,
  input  in_3,
  input  clk,
  output [15:0] A
);

  wire [15:0] add_1_s;

  Add #(.Bits(16)) add_1 (.a(A), .b(B), .c_i(1'b0), .s(add_1_s));  // open: c_o
  Register #(.Bits(16)) register_1 (.D(add_1_s), .C(clk), .en(in_3), .Q(A));
endmodule
