// Digital circuit test-3-yumen.dig as structural Verilog
module test_3_yumen (
  input  A,
  input  B,
  output C
);

  wire relay_1_p4;

  // Relay relay_1: pin names not known; wires that end beside it: A, 1'b1, 1'b0, relay_1_p4
  // Relay relay_2: pin names not known; wires that end beside it: B, relay_1_p4, 1'b0, C
  PullDown pulldown_1 (.out(C));
endmodule
