// Digital circuit test-4-huomen.dig as structural Verilog
module test_4_huomen (
  input  A,
  input  B,
  output C
);

  // Relay relay_1: pin names not known; wires that end beside it: 1'b1, C
  // Relay relay_2: pin names not known; wires that end beside it: A, 1'b1, B, 1'b0, C, 1'b0
  PullDown pulldown_1 (.out(C));
endmodule
