// Digital circuit test-6-与非门.dig as structural Verilog
module \test_6_与非门  (
  input  in_1,
  input  in_2,
  output out_3
);

  wire and_1_out;

  and and_1 (and_1_out, in_1, in_2);
  not not_1 (out_3, and_1_out);
endmodule
