// Digital circuit test-7-或非门.dig as structural Verilog
module \test_7_或非门  (
  input  in_1,
  input  in_2,
  output out_3
);

  wire or_1_out;

  or or_1 (or_1_out, in_1, in_2);
  not not_1 (out_3, or_1_out);
endmodule
